# Fritzing sketch Wiring I2C (saved by Fritzing 0.9.10b)

parts:
  Microcontroller = Arduino Nano Every THT
  OLED_Display = OLED 0.96" 128x64 I2C SSD1306
  JH2_0-13P = male pin header, 13 pins [form="♂ (male)"]

nets:
  N1: Microcontroller.Pin_2, OLED_Display.VCC
  N2: Microcontroller.Pin_8, OLED_Display.SCA
  N3: Microcontroller.Pin_9, OLED_Display.SCL
  N4: Microcontroller.Pin_14, Microcontroller.Pin_19, OLED_Display.GND, JH2_0-13P.pin2
  N5: Microcontroller.Pin_16, JH2_0-13P.pin3
  N6: Microcontroller.Pin_17, JH2_0-13P.pin4

custom parts:
  Arduino Nano Every THT: The Nano Every is Arduino’s 5V compatible board in the smallest available form factor: 45x18mm! The Arduino Nano is the preferred board for many projects requiring a small and easy to use microcontroller board. The small footprint and low price, make the Nano Every particularly suited for wearable inventions, low cost robotics, electronic musical instruments, and general use to control smaller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
