# Fritzing sketch Wiring SPI (saved by Fritzing 0.9.10b)

parts:
  Microcontroller = Arduino Nano Every THT
  JH2_0-13P = male pin header, 13 pins [form="♂ (male)"]
  Bauteil2 = SPI OLED Monochrome 128x64 0.96 inch

nets:
  N1: Microcontroller.Pin_2, Bauteil2.VDD
  N2: Microcontroller.Pin_3, Bauteil2.SCK
  N3: Microcontroller.Pin_14, Microcontroller.Pin_19, JH2_0-13P.pin2, Bauteil2.GND
  N4: Microcontroller.Pin_16, JH2_0-13P.pin3
  N5: Microcontroller.Pin_17, JH2_0-13P.pin4
  N6: Microcontroller.Pin_26, Microcontroller.Pin_27, Bauteil2.DC, Bauteil2.CS
  N7: Microcontroller.Pin_28, Bauteil2.RES
  N8: Microcontroller.Pin_30, Bauteil2.SDA

custom parts:
  Arduino Nano Every THT: The Nano Every is Arduino’s 5V compatible board in the smallest available form factor: 45x18mm! The Arduino Nano is the preferred board for many projects requiring a small and easy to use microcontroller board. The small footprint and low price, make the Nano Every particularly suited for wearable inventions, low cost robotics, electronic musical instruments, and general use to control smaller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
  SPI OLED Monochrome 128x64 0.96 inch: Unknown 128x64 0.96 inch 128x64 SPI Monochrome OLED display
